// Logisim project 4-bitmultibin_2.circ as structural Verilog: 5 circuits, main circuit main
module main (
  input  A0,
  input  A1,
  input  A2,
  input  A3,
  input  Negative,
  output negativ,
  output _128,
  output _64,
  output _32,
  output _16,
  output _8,
  output _4,
  output _2,
  output _1
);

  wire n4_bits_half_adder_1_s0, n4_bits_half_adder_1_s1, n4_bits_half_adder_1_s2, n4_bits_half_adder_1_s3,
       n4_bits_half_adder_1_s4, n8_bits_half_adder_1_s8;

  xor xor_1 (negativ, Negative, n8_bits_half_adder_1_s8);
  _4_bits_half_adder u_4_bits_half_adder_1 (
    .A0(A0), .A1(A1), .A2(A2), .A3(A3), .S4(n4_bits_half_adder_1_s4), .S3(n4_bits_half_adder_1_s3),
    .S2(n4_bits_half_adder_1_s2), .S1(n4_bits_half_adder_1_s1), .S0(n4_bits_half_adder_1_s0));
  _8_bits_half_adder u_8_bits_half_adder_1 (
    .Negativ(Negative), .A7(n4_bits_half_adder_1_s4), .A6(n4_bits_half_adder_1_s3),
    .A5(n4_bits_half_adder_1_s2), .A4(n4_bits_half_adder_1_s1), .A3(n4_bits_half_adder_1_s0), .A2(A1),
    .A1(A0), .A0(1'b0), .S8(n8_bits_half_adder_1_s8), .S7(_128), .S6(_64), .S5(_32), .S4(_16), .S2(_8),
    .S3(_4), .S1(_2), .S0(_1));

  // Notes on the sheet:
  //   Konstant
endmodule

module full_adder (
  input  A,
  input  B,
  input  C,
  output S,
  output C_1
);

  wire and_1_out, and_2_out, xor_1_out;

  xor xor_1 (xor_1_out, A, B);
  and and_1 (and_1_out, A, B);
  xor xor_2 (S, xor_1_out, C);
  and and_2 (and_2_out, xor_1_out, C);
  or or_1 (C_1, and_2_out, and_1_out);

  // Notes on the sheet:
  //   A+B
endmodule

module half_adder (
  input  A,
  input  B,
  output S,
  output C1
);

  xor xor_1 (S, A, B);
  and and_1 (C1, A, B);
endmodule

module _8_bits_half_adder (
  input  A7,
  input  A6,
  input  A5,
  input  A4,
  input  A3,
  input  A2,
  input  A1,
  input  A0,
  input  Negativ,
  output S8,
  output S7,
  output S6,
  output S5,
  output S4,
  output S2,
  output S3,
  output S1,
  output S0
);

  wire half_adder_2_c1, half_adder_3_c1, half_adder_4_c1, half_adder_5_c1, half_adder_6_c1, half_adder_7_c1,
       half_adder_8_c1, xor_1_out, xor_2_out, xor_3_out, xor_4_out, xor_5_out, xor_6_out, xor_7_out,
       xor_8_out;

  xor xor_1 (xor_1_out, A7, Negativ);
  half_adder half_adder_1 (.A(half_adder_2_c1), .B(xor_1_out), .S(S7), .C1(S8));
  xor xor_2 (xor_2_out, A6, Negativ);
  half_adder half_adder_2 (.A(half_adder_3_c1), .B(xor_2_out), .S(S6), .C1(half_adder_2_c1));
  xor xor_3 (xor_3_out, A5, Negativ);
  half_adder half_adder_3 (.A(half_adder_4_c1), .B(xor_3_out), .S(S5), .C1(half_adder_3_c1));
  xor xor_4 (xor_4_out, A4, Negativ);
  half_adder half_adder_4 (.A(half_adder_5_c1), .B(xor_4_out), .S(S4), .C1(half_adder_4_c1));
  xor xor_5 (xor_5_out, A3, Negativ);
  half_adder half_adder_5 (.A(half_adder_6_c1), .B(xor_5_out), .S(S2), .C1(half_adder_5_c1));
  xor xor_6 (xor_6_out, A2, Negativ);
  half_adder half_adder_6 (.A(half_adder_7_c1), .B(xor_6_out), .S(S3), .C1(half_adder_6_c1));
  xor xor_7 (xor_7_out, A1, Negativ);
  xor xor_8 (xor_8_out, A0, Negativ);
  half_adder half_adder_7 (.A(half_adder_8_c1), .B(xor_7_out), .S(S1), .C1(half_adder_7_c1));
  half_adder half_adder_8 (.A(Negativ), .B(xor_8_out), .S(S0), .C1(half_adder_8_c1));
endmodule

module _4_bits_half_adder (
  input  A0,
  input  A1,
  input  A2,
  input  A3,
  output S4,
  output S3,
  output S2,
  output S1,
  output S0
);

  wire full_adder_1_c_1, half_adder_2_c1, half_adder_3_c1;

  half_adder half_adder_1 (.A(half_adder_2_c1), .B(A3), .S(S3), .C1(S4));
  half_adder half_adder_2 (.A(full_adder_1_c_1), .B(A2), .S(S2), .C1(half_adder_2_c1));
  half_adder half_adder_3 (.A(A0), .B(A2), .S(S0), .C1(half_adder_3_c1));
  full_adder full_adder_1 (.A(half_adder_3_c1), .B(A1), .C(A3), .S(S1), .C_1(full_adder_1_c_1));

  // Notes on the sheet:
  //   FA
endmodule
